# Fritzing sketch CIRCUITO (saved by Fritzing 0.9.3b)
breadboards: 1

parts:
  Componente1 = Arduino Uno (Rev3)
  Raspberry_Pi_B_rev1 = Raspberry Pi B rev1
  R1 = Resistor [tolerance=±5% resistance=1k package=THT]
  R2 = Resistor [tolerance=±5% resistance=1k package=THT]
  2N2222A = NPN-Transistor [package="TO92 [THT]"]
  2N2222A1 = NPN-Transistor [package="TO92 [THT]"]
  R3 = Resistor [tolerance=±5% resistance=1k package=THT]
  R4 = Resistor [tolerance=±5% resistance=220 package=THT]
  R5 = Resistor [tolerance=±5% resistance=1k package=THT]
  R6 = Resistor [tolerance=±5% resistance=470 package=THT]
  JP1 = RCA [package=rca]  # not connected

nets:
  GND: Componente1.GND, Raspberry_Pi_B_rev1.GND, Raspberry_Pi_B_rev1.GPIO_14, Raspberry_Pi_B_rev1.GPIO_15, Raspberry_Pi_B_rev1.GPIO_4, Raspberry_Pi_B_rev1.GPIO_7, R1.Pin_1, R2.Pin_0, 2N2222A.E, R3.Pin_0, R3.Pin_1
  N1: Componente1.D0/RX, R1.Pin_0, 2N2222A1.C
  N2: Componente1.D1/TX, R4.Pin_0
  N3: Componente1.D7, R6.Pin_1
  N4: Componente1.5V, 2N2222A1.E
  3V3: Raspberry_Pi_B_rev1.3V3, Raspberry_Pi_B_rev1.5V, 2N2222A.C
  N5: R2.Pin_1, 2N2222A1.B
  N6: 2N2222A.B, R4.Pin_1
  N7: R5.Pin_0, R6.Pin_0
